// Logisim project xCPU-5.10.circ as structural Verilog
// 4 KWord Memory
module main (
);

  ALU alu_1 ();  // open: LD, CLK, AND, ADD, DR, INPR, COM, SHR, SHL, AC_0, AC_1, AC_2, AC_3, AC_4, AC_5, AC_6, AC_7, AC_8, AC_9, AC_10, AC_11, AC_12, AC_13, AC_14, AC_15, DR_0, DR_1, DR_2, DR_3, DR_4, DR_5, DR_6, DR_7, DR_8, DR_9, DR_10, DR_11, DR_12, DR_13, DR_14, DR_15, INPR_0, INPR_1, INPR_2, INPR_3, INPR_4, INPR_5, INPR_6, INPR_7, _0, _1, _2, _3, _4, _5, _6, _7, _8, _9, _10, _11, _12, _13, _14, _15
  Control_Unit control_unit_1 ();  // open: SC_INC, SC_CLR, D0, D1, D2, D3, D4, D5, D6, D7, T0, T1, T2, T3, T4, T5, T6, T7, T8, T9, T10, T11, T12, T13, T14, T15
  BUS_SELEC bus_selec_1 ();  // open: I, S, E, R, IEN, FGI, FGO, T0, T1, T2, T3, T4, T5, T6, D0, D1, D2, D3, D4, D5, D6, D7, AR, PC, DR, AC, IR, TR, MemRead
  AC ac_1 ();  // open: output, AC_15, AC_0, I, S, E, R, IEN, FGI, FGO, T0, T1, T2, T3, T4, T5, T6, D0, D1, D2, D3, D4, D5, D6, D7, B0, B1, B2, B3, B4, B5, B6, B7, B8, B9, B10, B11, B15, Input
  Memory memory_1 ();  // open: Address, AC_15, AC_0, I, S, E, R, IEN, FGI, FGO, T0, T1, T2, T3, T4, T5, T6, D0, D1, D2, D3, D4, D5, D6, D7, B0, B1, B2, B3, B4, B5, B6, B7, B8, B9, B10, B11, Data_in, Data_Out
  AR ar_1 ();  // open: output, AC_15, AC_0, I, S, E, R, IEN, FGI, FGO, T0, T1, T2, T3, T4, T5, T6, D0, D1, D2, D3, D4, D5, D6, D7, B0, B1, B2, B3, B4, B5, B6, B7, B8, B9, B10, B11, Input
  PC pc_1 ();  // open: output, AC_15, AC_0, I, S, E, R, IEN, FGI, FGO, T0, T1, T2, T3, T4, T5, T6, D0, D1, D2, D3, D4, D5, D6, D7, B0, B1, B2, B3, B4, B5, B6, B7, B8, B9, B10, B11, input
  DR dr_1 ();  // open: output, AC_15, AC_0, I, S, E, R, IEN, FGI, FGO, T0, T1, T2, T3, T4, T5, T6, D0, D1, D2, D3, D4, D5, D6, D7, B0, B1, B2, B3, B4, B5, B6, B7, B8, B9, B10, B11, Input
  INPR inpr_1 ();  // open: AC_15, AC_0, I, S, E, R, IEN, FGI, FGO, T0, T1, T2, T3, T4, T5, T6, D0, D1, D2, D3, D4, D5, D6, D7, B0, B1, B2, B3, B4, B5, B6, B7, B8, B9, B10, B11, input
  IR ir_1 ();  // open: output, AC_15, AC_0, I, S, E, R, IEN, FGI, FGO, T0, T1, T2, T3, T4, T5, T6, D0, D1, D2, D3, D4, D5, D6, D7, B0, B1, B2, B3, B4, B5, B6, B7, B8, B9, B10, B11, input
  TR tr_1 ();  // open: output, AC_15, AC_0, I, S, E, R, IEN, FGI, FGO, T0, T1, T2, T3, T4, T5, T6, D0, D1, D2, D3, D4, D5, D6, D7, B0, B1, B2, B3, B4, B5, B6, B7, B8, B9, B10, B11, input
  OUTR outr_1 ();  // open: output, AC_15, AC_0, I, S, E, R, IEN, FGI, FGO, T0, T1, T2, T3, T4, T5, T6, D0, D1, D2, D3, D4, D5, D6, D7, B0, B1, B2, B3, B4, B5, B6, B7, B8, B9, B10, B11
  _16_Bit_BUS u_16_bit_bus_1 ();
endmodule

module _1_Bit_A_Reg (
  input  J1,
  input  J2,
  input  K1,
  input  K2,
  input  K3,
  input  CLK,
  output OUTPUT
);

  wire or_1_out, or_2_out;

  or or_1 (or_1_out, J1, J2);
  or or_2 (or_2_out, K1, K2, K3);
  J_K_Flip_Flop j_k_ff_1 (.J(or_1_out), .clk(CLK), .K(or_2_out), .Q(OUTPUT));  // open: Qn, preset, en, reset
endmodule

// 12 Bit A REG (INC,LD,CLR)
module _12_Bit_A_Register (
  input  Clear,
  input  Load,
  input  Increment,
  input  I0,
  input  I1,
  input  I2,
  input  I3,
  input  I4,
  input  I5,
  input  I6,
  input  I7,
  input  I8,
  input  I9,
  input  I10,
  input  I11,
  input  CLK,
  output o0,
  output o1,
  output _02,
  output o3,
  output _04,
  output _05,
  output _06,
  output _07,
  output _08,
  output _09,
  output o10,
  output _011,
  output Cout
);

  wire and_1_out, and_2_out, and_3_out, and_4_out, and_5_out, and_6_out, and_7_out, and_8_out, and_9_out,
       and_10_out, and_11_out, and_12_out, and_13_out, and_14_out, and_15_out, and_16_out, and_17_out,
       and_18_out, and_19_out, and_20_out, and_21_out, and_22_out, and_23_out, and_24_out, and_25_out,
       and_26_out, and_27_out, and_28_out, and_29_out, and_30_out, and_31_out, and_32_out, and_33_out,
       and_34_out, and_35_out, and_36_out, and_37_out;

  and and_1 (and_1_out, ~Clear, Load);  // AND_Gate
  and and_2 (and_2_out, and_1_out, I0);
  and and_3 (and_3_out, and_1_out, ~I0);  // AND_Gate
  and and_4 (and_4_out, and_1_out, I1);
  and and_5 (and_5_out, and_1_out, ~I1);  // AND_Gate
  and and_6 (and_6_out, and_1_out, I2);
  and and_7 (and_7_out, and_1_out, ~I2);  // AND_Gate
  and and_8 (and_8_out, I3, and_1_out);
  and and_9 (and_9_out, and_1_out, ~I3);  // AND_Gate
  and and_10 (and_10_out, and_1_out, I4);
  and and_11 (and_11_out, and_1_out, ~I4);  // AND_Gate
  and and_12 (and_12_out, and_1_out, I5);
  and and_13 (and_13_out, and_1_out, ~I5);  // AND_Gate
  and and_14 (and_14_out, and_1_out, I6);
  and and_15 (and_15_out, and_1_out, ~I6);  // AND_Gate
  and and_16 (and_16_out, and_1_out, I7);
  and and_17 (and_17_out, and_1_out, ~I7);  // AND_Gate
  and and_18 (and_18_out, and_1_out, I8);
  and and_19 (and_19_out, and_1_out, ~I8);  // AND_Gate
  and and_20 (and_20_out, and_1_out, I9);
  and and_21 (and_21_out, and_1_out, ~I9);  // AND_Gate
  and and_22 (and_22_out, and_1_out, I10);
  and and_23 (and_23_out, and_1_out, ~I10);  // AND_Gate
  and and_24 (and_24_out, and_1_out, I11);
  and and_25 (and_25_out, and_1_out, ~I11);  // AND_Gate
  and and_26 (and_26_out, ~Clear, ~Load, Increment);  // AND_Gate
  _1_Bit_A_Reg u_1_bit_a_reg_1 (
    .J1(and_26_out), .J2(and_2_out), .K1(Clear), .K2(and_26_out), .K3(and_3_out), .CLK(CLK), .OUTPUT(o0));
  and and_27 (and_27_out, o0, and_26_out);
  _1_Bit_A_Reg u_1_bit_a_reg_2 (
    .J1(and_27_out), .J2(and_4_out), .K1(Clear), .K2(and_27_out), .K3(and_5_out), .CLK(CLK), .OUTPUT(o1));
  and and_28 (and_28_out, o1, and_27_out);
  _1_Bit_A_Reg u_1_bit_a_reg_3 (
    .J1(and_28_out), .J2(and_6_out), .K1(and_28_out), .K2(Clear), .K3(and_7_out), .CLK(CLK), .OUTPUT(_02));
  and and_29 (and_29_out, _02, and_28_out);
  _1_Bit_A_Reg u_1_bit_a_reg_4 (
    .J1(and_29_out), .J2(and_8_out), .K1(and_29_out), .K2(Clear), .K3(and_9_out), .CLK(CLK), .OUTPUT(o3));
  and and_30 (and_30_out, o3, and_29_out);
  _1_Bit_A_Reg u_1_bit_a_reg_5 (
    .J1(and_30_out), .J2(and_10_out), .K1(and_30_out), .K2(Clear), .K3(and_11_out), .CLK(CLK), .OUTPUT(_04));
  and and_31 (and_31_out, _04, and_30_out);
  _1_Bit_A_Reg u_1_bit_a_reg_6 (
    .J1(and_31_out), .J2(and_12_out), .K1(and_31_out), .K2(Clear), .K3(and_13_out), .CLK(CLK), .OUTPUT(_05));
  and and_32 (and_32_out, _05, and_31_out);
  _1_Bit_A_Reg u_1_bit_a_reg_7 (
    .J1(and_32_out), .J2(and_14_out), .K1(and_32_out), .K2(and_15_out), .K3(Clear), .CLK(CLK), .OUTPUT(_06));
  and and_33 (and_33_out, _06, and_32_out);
  _1_Bit_A_Reg u_1_bit_a_reg_8 (
    .J1(and_33_out), .J2(and_16_out), .K1(and_33_out), .K2(Clear), .K3(and_17_out), .CLK(CLK), .OUTPUT(_07));
  and and_34 (and_34_out, _07, and_33_out);
  _1_Bit_A_Reg u_1_bit_a_reg_9 (
    .J1(and_34_out), .J2(and_18_out), .K1(and_34_out), .K2(Clear), .K3(and_19_out), .CLK(CLK), .OUTPUT(_08));
  and and_35 (and_35_out, _08, and_34_out);
  _1_Bit_A_Reg u_1_bit_a_reg_10 (
    .J1(and_35_out), .J2(and_20_out), .K1(and_35_out), .K2(Clear), .K3(and_21_out), .CLK(CLK), .OUTPUT(_09));
  and and_36 (and_36_out, _09, and_35_out);
  _1_Bit_A_Reg u_1_bit_a_reg_11 (
    .J1(and_36_out), .J2(and_22_out), .K1(and_36_out), .K2(Clear), .K3(and_23_out), .CLK(CLK), .OUTPUT(o10));
  and and_37 (and_37_out, o10, and_36_out);
  _1_Bit_A_Reg u_1_bit_a_reg_12 (
    .J1(and_37_out), .J2(and_24_out), .K1(and_37_out), .K2(Clear), .K3(and_25_out), .CLK(CLK), .OUTPUT(_011));
  and and_38 (Cout, _011, CLK);
endmodule

// 16 Bit A REG (INC,LD,CLR)
module _16_Bit_A_Register (
  input  Clear,
  input  Load,
  input  Increment,
  input  i0,
  input  i1,
  input  i2,
  input  i3,
  input  i4,
  input  i5,
  input  i6,
  input  i7,
  input  i8,
  input  i9,
  input  i10,
  input  i11,
  input  i12,
  input  i13,
  input  i14,
  input  i15,
  input  Clk,
  output o0,
  output o1,
  output _02,
  output _03,
  output _04,
  output _05,
  output _06,
  output _07,
  output _08,
  output _09,
  output o10,
  output o11,
  output o12,
  output o13,
  output o14,
  output _015,
  output Eo
);

  wire and_1_out, and_2_out, and_3_out, and_4_out, and_5_out, and_6_out, and_7_out, and_8_out, and_9_out,
       and_10_out, and_11_out, and_12_out, and_13_out, and_14_out, and_15_out, and_16_out, and_17_out,
       and_18_out, and_19_out, and_20_out, and_21_out, and_22_out, and_23_out, and_24_out, and_25_out,
       and_26_out, and_27_out, and_28_out, and_29_out, and_30_out, and_31_out, and_32_out, and_33_out,
       and_34_out, and_35_out, and_36_out, and_37_out, and_38_out, and_39_out, and_40_out, and_41_out,
       and_42_out, and_43_out, and_44_out, and_45_out, and_46_out, and_47_out, and_48_out, and_49_out;

  and and_1 (and_1_out, ~Clear, Load);  // AND_Gate
  and and_2 (and_2_out, ~Clear, ~Load, Increment);  // AND_Gate
  and and_3 (and_3_out, and_1_out, i0);
  and and_4 (and_4_out, and_1_out, ~i0);  // AND_Gate
  and and_5 (and_5_out, and_1_out, i1);
  and and_6 (and_6_out, and_1_out, ~i1);  // AND_Gate
  and and_7 (and_7_out, and_1_out, i2);
  and and_8 (and_8_out, and_1_out, ~i2);  // AND_Gate
  and and_9 (and_9_out, and_1_out, i3);
  and and_10 (and_10_out, and_1_out, ~i3);  // AND_Gate
  and and_11 (and_11_out, and_1_out, i4);
  and and_12 (and_12_out, and_1_out, ~i4);  // AND_Gate
  and and_13 (and_13_out, and_1_out, i5);
  and and_14 (and_14_out, and_1_out, ~i5);  // AND_Gate
  and and_15 (and_15_out, and_1_out, i6);
  and and_16 (and_16_out, and_1_out, ~i6);  // AND_Gate
  and and_17 (and_17_out, and_1_out, i7);
  and and_18 (and_18_out, and_1_out, ~i7);  // AND_Gate
  and and_19 (and_19_out, and_1_out, i8);
  and and_20 (and_20_out, and_1_out, ~i8);  // AND_Gate
  and and_21 (and_21_out, and_1_out, i9);
  and and_22 (and_22_out, and_1_out, ~i9);  // AND_Gate
  and and_23 (and_23_out, and_1_out, i7);
  and and_24 (and_24_out, and_1_out, ~i7);  // AND_Gate
  and and_25 (and_25_out, and_1_out, i11);
  and and_26 (and_26_out, and_1_out, ~i11);  // AND_Gate
  and and_27 (and_27_out, and_1_out, i9);
  and and_28 (and_28_out, and_1_out, ~i9);  // AND_Gate
  and and_29 (and_29_out, and_1_out, i13);
  and and_30 (and_30_out, and_1_out, ~i13);  // AND_Gate
  and and_31 (and_31_out, and_1_out, i14);
  and and_32 (and_32_out, and_1_out, ~i14);  // AND_Gate
  and and_33 (and_33_out, and_1_out, i15);
  and and_34 (and_34_out, and_1_out, ~i15);  // AND_Gate
  _1_Bit_A_Reg u_1_bit_a_reg_1 (
    .J1(and_2_out), .J2(and_3_out), .K1(and_4_out), .K2(and_2_out), .K3(Clear), .CLK(Clk), .OUTPUT(o0));
  and and_35 (and_35_out, and_2_out, o0);
  _1_Bit_A_Reg u_1_bit_a_reg_2 (
    .J1(and_35_out), .J2(and_5_out), .K1(and_35_out), .K2(Clear), .K3(and_6_out), .CLK(Clk), .OUTPUT(o1));
  and and_36 (and_36_out, and_35_out, o1);
  _1_Bit_A_Reg u_1_bit_a_reg_3 (
    .J1(and_36_out), .J2(and_7_out), .K1(and_36_out), .K2(Clear), .K3(and_8_out), .CLK(Clk), .OUTPUT(_02));
  and and_37 (and_37_out, and_36_out, _02);
  _1_Bit_A_Reg u_1_bit_a_reg_4 (
    .J1(and_37_out), .J2(and_9_out), .K1(and_37_out), .K2(Clear), .K3(and_10_out), .CLK(Clk), .OUTPUT(_03));
  and and_38 (and_38_out, and_37_out, _03);
  _1_Bit_A_Reg u_1_bit_a_reg_5 (
    .J1(and_38_out), .J2(and_11_out), .K1(and_38_out), .K2(Clear), .K3(and_12_out), .CLK(Clk), .OUTPUT(_04));
  and and_39 (and_39_out, and_38_out, _04);
  _1_Bit_A_Reg u_1_bit_a_reg_6 (
    .J1(and_39_out), .J2(and_13_out), .K1(and_39_out), .K2(Clear), .K3(and_14_out), .CLK(Clk), .OUTPUT(_05));
  and and_40 (and_40_out, and_39_out, _05);
  _1_Bit_A_Reg u_1_bit_a_reg_7 (
    .J1(and_40_out), .J2(and_15_out), .K1(and_40_out), .K2(Clear), .K3(and_16_out), .CLK(Clk), .OUTPUT(_06));
  and and_41 (and_41_out, and_40_out, _06);
  _1_Bit_A_Reg u_1_bit_a_reg_8 (
    .J1(and_41_out), .J2(and_17_out), .K1(and_41_out), .K2(Clear), .K3(and_18_out), .CLK(Clk), .OUTPUT(_07));
  and and_42 (and_42_out, and_41_out, _07);
  _1_Bit_A_Reg u_1_bit_a_reg_9 (
    .J1(and_42_out), .J2(and_19_out), .K1(and_42_out), .K2(Clear), .K3(and_20_out), .CLK(Clk), .OUTPUT(_08));
  and and_43 (and_43_out, and_42_out, _08);
  _1_Bit_A_Reg u_1_bit_a_reg_10 (
    .J1(and_43_out), .J2(and_21_out), .K1(and_43_out), .K2(Clear), .K3(and_22_out), .CLK(Clk), .OUTPUT(_09));
  and and_44 (and_44_out, and_43_out, _09);
  _1_Bit_A_Reg u_1_bit_a_reg_11 (
    .J1(and_44_out), .J2(and_23_out), .K1(and_44_out), .K2(Clear), .K3(and_24_out), .CLK(Clk), .OUTPUT(o10));
  and and_45 (and_45_out, and_44_out, o10);
  _1_Bit_A_Reg u_1_bit_a_reg_12 (
    .J1(and_45_out), .J2(and_25_out), .K1(and_45_out), .K2(Clear), .K3(and_26_out), .CLK(Clk), .OUTPUT(o11));
  and and_46 (and_46_out, and_45_out, o11);
  _1_Bit_A_Reg u_1_bit_a_reg_13 (
    .J1(and_46_out), .J2(and_27_out), .K1(and_46_out), .K2(Clear), .K3(and_28_out), .CLK(Clk), .OUTPUT(o12));
  and and_47 (and_47_out, and_46_out, o12);
  _1_Bit_A_Reg u_1_bit_a_reg_14 (
    .J1(and_47_out), .J2(and_29_out), .K1(and_47_out), .K2(Clear), .K3(and_30_out), .CLK(Clk), .OUTPUT(o13));
  and and_48 (and_48_out, and_47_out, o13);
  _1_Bit_A_Reg u_1_bit_a_reg_15 (
    .J1(and_48_out), .J2(and_31_out), .K1(and_48_out), .K2(Clear), .K3(and_32_out), .CLK(Clk), .OUTPUT(o14));
  and and_49 (and_49_out, and_48_out, o14);
  _1_Bit_A_Reg u_1_bit_a_reg_16 (
    .J1(and_49_out), .J2(and_33_out), .K1(and_49_out), .K2(Clear), .K3(and_34_out), .CLK(Clk), .OUTPUT(_015));
  and and_50 (Eo, and_49_out, _015);

  assign i10 = i7;
  assign i12 = i9;
endmodule

module _1_Bit_B_Reg (
  input  Load_prime_input,
  input  Load_prime_prime_input,
  input  Data_in,
  input  CLK,
  output Data_out,
  output Load_prime_output,
  output Load_prime_prime_out
);

  wire and_1_out, and_2_out, or_1_out;

  and and_1 (and_1_out, Data_out, Load_prime_input);
  and and_2 (and_2_out, Load_prime_prime_input, Data_in);
  or or_1 (or_1_out, and_1_out, and_2_out);
  D_Flip_Flop d_ff_1 (.clk(CLK), .D(or_1_out), .Q(Data_out));  // open: Qn, preset, en, reset

  assign Load_prime_output = Load_prime_input;
  assign Load_prime_prime_out = Load_prime_prime_input;
endmodule

// 8 Bit B REG
module _8_Bit_B_Reg (
  input  Load,
  input  i0,
  input  i1,
  input  i2,
  input  i3,
  input  i4,
  input  i5,
  input  i6,
  input  i7,
  input  Clock,
  output o0,
  output o1,
  output o2,
  output o3,
  output _04,
  output o5,
  output o6,
  output o7
);

  wire n1_bit_b_reg_1_load_prime_output, n1_bit_b_reg_1_load_prime_prime_out,
       n1_bit_b_reg_2_load_prime_output, n1_bit_b_reg_2_load_prime_prime_out,
       n1_bit_b_reg_3_load_prime_output, n1_bit_b_reg_3_load_prime_prime_out,
       n1_bit_b_reg_4_load_prime_output, n1_bit_b_reg_4_load_prime_prime_out,
       n1_bit_b_reg_5_load_prime_output, n1_bit_b_reg_5_load_prime_prime_out,
       n1_bit_b_reg_6_load_prime_output, n1_bit_b_reg_6_load_prime_prime_out,
       n1_bit_b_reg_7_load_prime_output, n1_bit_b_reg_7_load_prime_prime_out, not_1_out, not_2_out;

  not not_1 (not_1_out, not_2_out);
  not not_2 (not_2_out, Load);
  _1_Bit_B_Reg u_1_bit_b_reg_1 (
    .Data_in(i0), .Load_prime_input(not_2_out), .Load_prime_prime_input(not_1_out),
    .Load_prime_output(n1_bit_b_reg_1_load_prime_output),
    .Load_prime_prime_out(n1_bit_b_reg_1_load_prime_prime_out), .CLK(Clock), .Data_out(o0));
  _1_Bit_B_Reg u_1_bit_b_reg_2 (
    .Data_in(i1), .Load_prime_input(n1_bit_b_reg_1_load_prime_output),
    .Load_prime_prime_input(n1_bit_b_reg_1_load_prime_prime_out),
    .Load_prime_output(n1_bit_b_reg_2_load_prime_output),
    .Load_prime_prime_out(n1_bit_b_reg_2_load_prime_prime_out), .CLK(Clock), .Data_out(o1));
  _1_Bit_B_Reg u_1_bit_b_reg_3 (
    .Data_in(i2), .Load_prime_input(n1_bit_b_reg_2_load_prime_output),
    .Load_prime_prime_input(n1_bit_b_reg_2_load_prime_prime_out),
    .Load_prime_output(n1_bit_b_reg_3_load_prime_output),
    .Load_prime_prime_out(n1_bit_b_reg_3_load_prime_prime_out), .CLK(Clock), .Data_out(o2));
  _1_Bit_B_Reg u_1_bit_b_reg_4 (
    .Data_in(i3), .Load_prime_input(n1_bit_b_reg_3_load_prime_output),
    .Load_prime_prime_input(n1_bit_b_reg_3_load_prime_prime_out),
    .Load_prime_output(n1_bit_b_reg_4_load_prime_output),
    .Load_prime_prime_out(n1_bit_b_reg_4_load_prime_prime_out), .CLK(Clock), .Data_out(o3));
  _1_Bit_B_Reg u_1_bit_b_reg_5 (
    .Data_in(i4), .Load_prime_input(n1_bit_b_reg_4_load_prime_output),
    .Load_prime_prime_input(n1_bit_b_reg_4_load_prime_prime_out),
    .Load_prime_output(n1_bit_b_reg_5_load_prime_output),
    .Load_prime_prime_out(n1_bit_b_reg_5_load_prime_prime_out), .CLK(Clock), .Data_out(_04));
  _1_Bit_B_Reg u_1_bit_b_reg_6 (
    .Data_in(i5), .Load_prime_input(n1_bit_b_reg_5_load_prime_output),
    .Load_prime_prime_input(n1_bit_b_reg_5_load_prime_prime_out),
    .Load_prime_output(n1_bit_b_reg_6_load_prime_output),
    .Load_prime_prime_out(n1_bit_b_reg_6_load_prime_prime_out), .CLK(Clock), .Data_out(o5));
  _1_Bit_B_Reg u_1_bit_b_reg_7 (
    .Data_in(i6), .Load_prime_input(n1_bit_b_reg_6_load_prime_output),
    .Load_prime_prime_input(n1_bit_b_reg_6_load_prime_prime_out),
    .Load_prime_output(n1_bit_b_reg_7_load_prime_output),
    .Load_prime_prime_out(n1_bit_b_reg_7_load_prime_prime_out), .CLK(Clock), .Data_out(o6));
  _1_Bit_B_Reg u_1_bit_b_reg_8 (
    .Data_in(i7), .Load_prime_input(n1_bit_b_reg_7_load_prime_output),
    .Load_prime_prime_input(n1_bit_b_reg_7_load_prime_prime_out), .CLK(Clock), .Data_out(o7));  // open: Load_prime_output, Load_prime_prime_out
endmodule

// 16 Bit REG
module _16_Bit_B_Reg (
  input  Load,
  input  i0,
  input  i1,
  input  i2,
  input  i3,
  input  i4,
  input  i5,
  input  i6,
  input  i7,
  input  i8,
  input  i9,
  input  i10,
  input  i11,
  input  i12,
  input  i13,
  input  i14,
  input  i15,
  input  Clock,
  output o0,
  output o1,
  output o2,
  output o3,
  output _04,
  output o5,
  output o6,
  output o7,
  output o8,
  output o9,
  output o10,
  output o11,
  output o12,
  output o13,
  output o14,
  output o15
);

  wire n1_bit_b_reg_1_load_prime_output, n1_bit_b_reg_1_load_prime_prime_out,
       n1_bit_b_reg_2_load_prime_output, n1_bit_b_reg_2_load_prime_prime_out,
       n1_bit_b_reg_3_load_prime_output, n1_bit_b_reg_3_load_prime_prime_out,
       n1_bit_b_reg_4_load_prime_output, n1_bit_b_reg_4_load_prime_prime_out,
       n1_bit_b_reg_5_load_prime_output, n1_bit_b_reg_5_load_prime_prime_out,
       n1_bit_b_reg_6_load_prime_output, n1_bit_b_reg_6_load_prime_prime_out,
       n1_bit_b_reg_7_load_prime_output, n1_bit_b_reg_7_load_prime_prime_out,
       n1_bit_b_reg_8_load_prime_output, n1_bit_b_reg_8_load_prime_prime_out,
       n1_bit_b_reg_9_load_prime_output, n1_bit_b_reg_9_load_prime_prime_out,
       n1_bit_b_reg_10_load_prime_output, n1_bit_b_reg_10_load_prime_prime_out,
       n1_bit_b_reg_11_load_prime_output, n1_bit_b_reg_11_load_prime_prime_out,
       n1_bit_b_reg_12_load_prime_output, n1_bit_b_reg_12_load_prime_prime_out,
       n1_bit_b_reg_13_load_prime_output, n1_bit_b_reg_13_load_prime_prime_out,
       n1_bit_b_reg_14_load_prime_output, n1_bit_b_reg_14_load_prime_prime_out,
       n1_bit_b_reg_15_load_prime_output, n1_bit_b_reg_15_load_prime_prime_out, not_1_out, not_2_out;

  not not_1 (not_1_out, not_2_out);
  not not_2 (not_2_out, Load);
  _1_Bit_B_Reg u_1_bit_b_reg_1 (
    .Data_in(i0), .Load_prime_input(not_2_out), .Load_prime_prime_input(not_1_out),
    .Load_prime_output(n1_bit_b_reg_1_load_prime_output),
    .Load_prime_prime_out(n1_bit_b_reg_1_load_prime_prime_out), .CLK(Clock), .Data_out(o0));
  _1_Bit_B_Reg u_1_bit_b_reg_2 (
    .Data_in(i1), .Load_prime_input(n1_bit_b_reg_1_load_prime_output),
    .Load_prime_prime_input(n1_bit_b_reg_1_load_prime_prime_out),
    .Load_prime_output(n1_bit_b_reg_2_load_prime_output),
    .Load_prime_prime_out(n1_bit_b_reg_2_load_prime_prime_out), .CLK(Clock), .Data_out(o1));
  _1_Bit_B_Reg u_1_bit_b_reg_3 (
    .Data_in(i2), .Load_prime_input(n1_bit_b_reg_2_load_prime_output),
    .Load_prime_prime_input(n1_bit_b_reg_2_load_prime_prime_out),
    .Load_prime_output(n1_bit_b_reg_3_load_prime_output),
    .Load_prime_prime_out(n1_bit_b_reg_3_load_prime_prime_out), .CLK(Clock), .Data_out(o2));
  _1_Bit_B_Reg u_1_bit_b_reg_4 (
    .Data_in(i3), .Load_prime_input(n1_bit_b_reg_3_load_prime_output),
    .Load_prime_prime_input(n1_bit_b_reg_3_load_prime_prime_out),
    .Load_prime_output(n1_bit_b_reg_4_load_prime_output),
    .Load_prime_prime_out(n1_bit_b_reg_4_load_prime_prime_out), .CLK(Clock), .Data_out(o3));
  _1_Bit_B_Reg u_1_bit_b_reg_5 (
    .Data_in(i4), .Load_prime_input(n1_bit_b_reg_4_load_prime_output),
    .Load_prime_prime_input(n1_bit_b_reg_4_load_prime_prime_out),
    .Load_prime_output(n1_bit_b_reg_5_load_prime_output),
    .Load_prime_prime_out(n1_bit_b_reg_5_load_prime_prime_out), .CLK(Clock), .Data_out(_04));
  _1_Bit_B_Reg u_1_bit_b_reg_6 (
    .Data_in(i5), .Load_prime_input(n1_bit_b_reg_5_load_prime_output),
    .Load_prime_prime_input(n1_bit_b_reg_5_load_prime_prime_out),
    .Load_prime_output(n1_bit_b_reg_6_load_prime_output),
    .Load_prime_prime_out(n1_bit_b_reg_6_load_prime_prime_out), .CLK(Clock), .Data_out(o5));
  _1_Bit_B_Reg u_1_bit_b_reg_7 (
    .Data_in(i6), .Load_prime_input(n1_bit_b_reg_6_load_prime_output),
    .Load_prime_prime_input(n1_bit_b_reg_6_load_prime_prime_out),
    .Load_prime_output(n1_bit_b_reg_7_load_prime_output),
    .Load_prime_prime_out(n1_bit_b_reg_7_load_prime_prime_out), .CLK(Clock), .Data_out(o6));
  _1_Bit_B_Reg u_1_bit_b_reg_8 (
    .Data_in(i7), .Load_prime_input(n1_bit_b_reg_7_load_prime_output),
    .Load_prime_prime_input(n1_bit_b_reg_7_load_prime_prime_out),
    .Load_prime_output(n1_bit_b_reg_8_load_prime_output),
    .Load_prime_prime_out(n1_bit_b_reg_8_load_prime_prime_out), .CLK(Clock), .Data_out(o7));
  _1_Bit_B_Reg u_1_bit_b_reg_9 (
    .Data_in(i8), .Load_prime_input(n1_bit_b_reg_8_load_prime_output),
    .Load_prime_prime_input(n1_bit_b_reg_8_load_prime_prime_out),
    .Load_prime_output(n1_bit_b_reg_9_load_prime_output),
    .Load_prime_prime_out(n1_bit_b_reg_9_load_prime_prime_out), .CLK(Clock), .Data_out(o8));
  _1_Bit_B_Reg u_1_bit_b_reg_10 (
    .Data_in(i9), .Load_prime_input(n1_bit_b_reg_9_load_prime_output),
    .Load_prime_prime_input(n1_bit_b_reg_9_load_prime_prime_out),
    .Load_prime_output(n1_bit_b_reg_10_load_prime_output),
    .Load_prime_prime_out(n1_bit_b_reg_10_load_prime_prime_out), .CLK(Clock), .Data_out(o9));
  _1_Bit_B_Reg u_1_bit_b_reg_11 (
    .Data_in(i10), .Load_prime_input(n1_bit_b_reg_10_load_prime_output),
    .Load_prime_prime_input(n1_bit_b_reg_10_load_prime_prime_out),
    .Load_prime_output(n1_bit_b_reg_11_load_prime_output),
    .Load_prime_prime_out(n1_bit_b_reg_11_load_prime_prime_out), .CLK(Clock), .Data_out(o10));
  _1_Bit_B_Reg u_1_bit_b_reg_12 (
    .Data_in(i11), .Load_prime_input(n1_bit_b_reg_11_load_prime_output),
    .Load_prime_prime_input(n1_bit_b_reg_11_load_prime_prime_out),
    .Load_prime_output(n1_bit_b_reg_12_load_prime_output),
    .Load_prime_prime_out(n1_bit_b_reg_12_load_prime_prime_out), .CLK(Clock), .Data_out(o11));
  _1_Bit_B_Reg u_1_bit_b_reg_13 (
    .Data_in(i12), .Load_prime_input(n1_bit_b_reg_12_load_prime_output),
    .Load_prime_prime_input(n1_bit_b_reg_12_load_prime_prime_out),
    .Load_prime_output(n1_bit_b_reg_13_load_prime_output),
    .Load_prime_prime_out(n1_bit_b_reg_13_load_prime_prime_out), .CLK(Clock), .Data_out(o12));
  _1_Bit_B_Reg u_1_bit_b_reg_14 (
    .Data_in(i13), .Load_prime_input(n1_bit_b_reg_13_load_prime_output),
    .Load_prime_prime_input(n1_bit_b_reg_13_load_prime_prime_out),
    .Load_prime_output(n1_bit_b_reg_14_load_prime_output),
    .Load_prime_prime_out(n1_bit_b_reg_14_load_prime_prime_out), .CLK(Clock), .Data_out(o13));
  _1_Bit_B_Reg u_1_bit_b_reg_15 (
    .Data_in(i14), .Load_prime_input(n1_bit_b_reg_14_load_prime_output),
    .Load_prime_prime_input(n1_bit_b_reg_14_load_prime_prime_out),
    .Load_prime_output(n1_bit_b_reg_15_load_prime_output),
    .Load_prime_prime_out(n1_bit_b_reg_15_load_prime_prime_out), .CLK(Clock), .Data_out(o14));
  _1_Bit_B_Reg u_1_bit_b_reg_16 (
    .Data_in(i15), .Load_prime_input(n1_bit_b_reg_15_load_prime_output),
    .Load_prime_prime_input(n1_bit_b_reg_15_load_prime_prime_out), .CLK(Clock), .Data_out(o15));  // open: Load_prime_output, Load_prime_prime_out
endmodule

// 16-Bit BUS
module _16_Bit_BUS (
);

  wire [2:0] bus_selec_1_ar;

  BUS_SELEC bus_selec_1 (
    .AR(bus_selec_1_ar[0]), .PC(bus_selec_1_ar[1]), .DR(bus_selec_1_ar[2]));  // open: I, S, E, R, IEN, FGI, FGO, T0, T1, T2, T3, T4, T5, T6, D0, D1, D2, D3, D4, D5, D6, D7, AC, IR, TR, MemRead
  _1_Ortak_bsus u_1_ortak_bsus_1 (.Select(bus_selec_1_ar));  // open: _0, _2, _3, _4, _5, _6, _7, _0_2, _1_2, _2_2, _3_2, _4_2, _5_2, _6_2, _7_2, _1
  _1_Ortak_bsus u_1_ortak_bsus_2 (.Select(bus_selec_1_ar));  // open: _0, _2, _3, _4, _5, _6, _7, _0_2, _1_2, _2_2, _3_2, _4_2, _5_2, _6_2, _7_2, _1
  _1_Ortak_bsus u_1_ortak_bsus_3 (.Select(bus_selec_1_ar));  // open: _0, _2, _3, _4, _5, _6, _7, _0_2, _1_2, _2_2, _3_2, _4_2, _5_2, _6_2, _7_2, _1
  _1_Ortak_bsus u_1_ortak_bsus_4 (.Select(bus_selec_1_ar));  // open: _0, _2, _3, _4, _5, _6, _7, _0_2, _1_2, _2_2, _3_2, _4_2, _5_2, _6_2, _7_2, _1
  _1_Ortak_bsus u_1_ortak_bsus_5 (.Select(bus_selec_1_ar));  // open: _0, _2, _3, _4, _5, _6, _7, _0_2, _1_2, _2_2, _3_2, _4_2, _5_2, _6_2, _7_2, _1
  _1_Ortak_bsus u_1_ortak_bsus_6 (.Select(bus_selec_1_ar));  // open: _0, _2, _3, _4, _5, _6, _7, _0_2, _1_2, _2_2, _3_2, _4_2, _5_2, _6_2, _7_2, _1
  _1_Ortak_bsus u_1_ortak_bsus_7 (.Select(bus_selec_1_ar));  // open: _0, _2, _3, _4, _5, _6, _7, _0_2, _1_2, _2_2, _3_2, _4_2, _5_2, _6_2, _7_2, _1
  _1_Ortak_bsus u_1_ortak_bsus_8 (.Select(bus_selec_1_ar));  // open: _0, _2, _3, _4, _5, _6, _7, _0_2, _1_2, _2_2, _3_2, _4_2, _5_2, _6_2, _7_2, _1
  _1_Ortak_bsus u_1_ortak_bsus_9 (.Select(bus_selec_1_ar));  // open: _0, _2, _3, _4, _5, _6, _7, _0_2, _1_2, _2_2, _3_2, _4_2, _5_2, _6_2, _7_2, _1
  _1_Ortak_bsus u_1_ortak_bsus_10 (.Select(bus_selec_1_ar));  // open: _0, _2, _3, _4, _5, _6, _7, _0_2, _1_2, _2_2, _3_2, _4_2, _5_2, _6_2, _7_2, _1
  _1_Ortak_bsus u_1_ortak_bsus_11 (.Select(bus_selec_1_ar));  // open: _0, _2, _3, _4, _5, _6, _7, _0_2, _1_2, _2_2, _3_2, _4_2, _5_2, _6_2, _7_2, _1
  _1_Ortak_bsus u_1_ortak_bsus_12 (.Select(bus_selec_1_ar));  // open: _0, _2, _3, _4, _5, _6, _7, _0_2, _1_2, _2_2, _3_2, _4_2, _5_2, _6_2, _7_2, _1
  _1_Ortak_bsus u_1_ortak_bsus_13 (.Select(bus_selec_1_ar));  // open: _0, _2, _3, _4, _5, _6, _7, _0_2, _1_2, _2_2, _3_2, _4_2, _5_2, _6_2, _7_2, _1
  _1_Ortak_bsus u_1_ortak_bsus_14 (.Select(bus_selec_1_ar));  // open: _0, _2, _3, _4, _5, _6, _7, _0_2, _1_2, _2_2, _3_2, _4_2, _5_2, _6_2, _7_2, _1
  _1_Ortak_bsus u_1_ortak_bsus_15 (.Select(bus_selec_1_ar));  // open: _0, _2, _3, _4, _5, _6, _7, _0_2, _1_2, _2_2, _3_2, _4_2, _5_2, _6_2, _7_2, _1
  _1_Ortak_bsus u_1_ortak_bsus_16 (.Select(bus_selec_1_ar));  // open: _0, _2, _3, _4, _5, _6, _7, _0_2, _1_2, _2_2, _3_2, _4_2, _5_2, _6_2, _7_2, _1
  AR ar_1 ();  // open: output, AC_15, AC_0, I, S, E, R, IEN, FGI, FGO, T0, T1, T2, T3, T4, T5, T6, D0, D1, D2, D3, D4, D5, D6, D7, B0, B1, B2, B3, B4, B5, B6, B7, B8, B9, B10, B11, Input
endmodule

module AR (
  input  AC_15,
  input  AC_0,
  input  I,
  input  S,
  input  E,
  input  R,
  input  IEN,
  input  FGI,
  input  FGO,
  input  T0,
  input  T1,
  input  T2,
  input  T3,
  input  T4,
  input  T5,
  input  T6,
  input  D0,
  input  D1,
  input  D2,
  input  D3,
  input  D4,
  input  D5,
  input  D6,
  input  D7,
  input  B0,
  input  B1,
  input  B2,
  input  B3,
  input  B4,
  input  B5,
  input  B6,
  input  B7,
  input  B8,
  input  B9,
  input  B10,
  input  B11,
  input  [11:0] Input,
  output [11:0] \output 
);

  wire and_1_out, and_2_out, and_3_out, and_4_out, and_5_out, clock_1_out, or_1_out;

  Clock clock_1 (.out(clock_1_out));
  and and_1 (and_1_out, R, T0);
  and and_2 (and_2_out, ~R, T0);  // AND_Gate
  and and_3 (and_3_out, ~R, T2);  // AND_Gate
  and and_4 (and_4_out, I, T3, ~D7);  // AND_Gate
  and and_5 (and_5_out, T4, D5);
  or or_1 (or_1_out, and_2_out, and_3_out, and_4_out);
  _12_Bit_A_Register u_12_bit_a_register_1 (
    .Clear(and_1_out), .Load(or_1_out), .Increment(and_5_out), .I0(Input[0]), .I1(Input[1]), .I2(Input[2]),
    .I3(Input[3]), .I4(Input[4]), .I5(Input[5]), .I6(Input[6]), .I7(Input[7]), .I8(Input[8]), .I9(Input[9]),
    .I10(Input[10]), .I11(Input[11]), .CLK(clock_1_out), .o0(\output [0]), .o1(\output [1]),
    ._02(\output [2]), .o3(\output [3]), ._04(\output [4]), ._05(\output [5]), ._06(\output [6]),
    ._07(\output [7]), ._08(\output [8]), ._09(\output [9]), .o10(\output [10]), ._011(\output [11]));  // open: Cout

  // Notes on the sheet:
  //   CLR=R*T0
  //   R'*T0
  //   D7'*I*T3
  //   INC=D5*T4
  //   LD=R'*T0+R'*T2+D7'*I*T3
endmodule

module PC (
  input  AC_15,
  input  AC_0,
  input  I,
  input  S,
  input  E,
  input  R,
  input  IEN,
  input  FGI,
  input  FGO,
  input  T0,
  input  T1,
  input  T2,
  input  T3,
  input  T4,
  input  T5,
  input  T6,
  input  D0,
  input  D1,
  input  D2,
  input  D3,
  input  D4,
  input  D5,
  input  D6,
  input  D7,
  input  B0,
  input  B1,
  input  B2,
  input  B3,
  input  B4,
  input  B5,
  input  B6,
  input  B7,
  input  B8,
  input  B9,
  input  B10,
  input  B11,
  input  [11:0] \input ,
  output [11:0] \output 
);

  wire and_1_out, and_2_out, and_3_out, and_4_out, and_5_out, and_6_out, and_7_out, and_8_out, and_9_out,
       and_10_out, and_11_out, and_12_out, and_13_out, and_14_out, and_15_out, and_16_out, and_17_out,
       clock_1_out, not_1_out, not_2_out, not_3_out, or_1_out, or_2_out;

  Clock clock_1 (.out(clock_1_out));
  and and_1 (and_1_out, R, T1);
  and and_2 (and_2_out, T4, D4);
  and and_3 (and_3_out, T5, D5);
  not not_1 (not_1_out, I);
  or or_1 (or_1_out, and_2_out, and_3_out);
  and and_4 (and_4_out, not_1_out, T3, D7);
  not not_2 (not_2_out, AC_0);
  not not_3 (not_3_out, AC_15);
  and and_5 (and_5_out, and_4_out, B4);
  and and_6 (and_6_out, and_4_out, B3);
  and and_7 (and_7_out, and_4_out, B2);
  and and_8 (and_8_out, and_4_out, B1);
  and and_9 (and_9_out, I, T3, D7);
  and and_10 (and_10_out, and_9_out, B8);
  and and_11 (and_11_out, and_5_out, not_3_out);
  and and_12 (and_12_out, and_6_out, AC_15);
  and and_13 (and_13_out, and_7_out, not_2_out);
  and and_14 (and_14_out, and_8_out, E);
  and and_15 (and_15_out, FGI, and_16_out);
  and and_16 (and_16_out, and_9_out, B9);
  and and_17 (and_17_out, FGO, and_10_out);
  or or_2 (or_2_out, and_11_out, and_12_out, and_13_out, and_14_out, and_15_out, and_17_out);
  _12_Bit_A_Register u_12_bit_a_register_1 (
    .Clear(and_1_out), .Load(or_1_out), .Increment(or_2_out), .I0(\input [0]), .I1(\input [1]),
    .I2(\input [2]), .I3(\input [3]), .I4(\input [4]), .I5(\input [5]), .I6(\input [6]), .I7(\input [7]),
    .I8(\input [8]), .I9(\input [9]), .I10(\input [10]), .I11(\input [11]), .CLK(clock_1_out),
    .o0(\output [0]), .o1(\output [1]), ._02(\output [2]), .o3(\output [3]), ._04(\output [4]),
    ._05(\output [5]), ._06(\output [6]), ._07(\output [7]), ._08(\output [8]), ._09(\output [9]),
    .o10(\output [10]), ._011(\output [11]));  // open: Cout

  // Notes on the sheet:
  //   CLR= R*T1
  //   r=D7 I' T3
  //   p=D7*I*T3
  //   LD=D4*T4+D5*T5
  //   r*B4*AC(15)'
  //   r*B3*AC(15)
  //   r*B2*AC(0)'
  //   r*B1*E
  //   p B9 FGI
  //   p B8 FG0
  //   DR'D6T6p girişi için tekrar kontrol et
  //   INC=r*B4*AC(15)'+r*B3*AC(15)+r*B2*AC(0)'+r*B1*E+p*B9*FGI +p*B8*FG0
endmodule

module DR (
  input  AC_15,
  input  AC_0,
  input  I,
  input  S,
  input  E,
  input  R,
  input  IEN,
  input  FGI,
  input  FGO,
  input  T0,
  input  T1,
  input  T2,
  input  T3,
  input  T4,
  input  T5,
  input  T6,
  input  D0,
  input  D1,
  input  D2,
  input  D3,
  input  D4,
  input  D5,
  input  D6,
  input  D7,
  input  B0,
  input  B1,
  input  B2,
  input  B3,
  input  B4,
  input  B5,
  input  B6,
  input  B7,
  input  B8,
  input  B9,
  input  B10,
  input  B11,
  input  [15:0] Input,
  output [15:0] \output 
);

  wire and_1_out, and_2_out, clock_1_out, or_1_out;

  Clock clock_1 (.out(clock_1_out));
  or or_1 (or_1_out, D0, D1, D2, D6);
  and and_1 (and_1_out, T5, D6);
  and and_2 (and_2_out, T4, or_1_out);
  _16_Bit_A_Register u_16_bit_a_register_1 (
    .Clear(1'b0), .Load(and_2_out), .Increment(and_1_out), .i0(Input[0]), .i1(Input[1]), .i2(Input[2]),
    .i3(Input[3]), .i4(Input[4]), .i5(Input[5]), .i6(Input[6]), .i7(Input[7]), .i8(Input[8]), .i9(Input[9]),
    .i10(Input[10]), .i11(Input[11]), .i12(Input[12]), .i13(Input[13]), .i14(Input[14]), .i15(Input[15]),
    .Clk(clock_1_out), .o0(\output [0]), .o1(\output [1]), ._02(\output [2]), ._03(\output [3]),
    ._04(\output [4]), ._05(\output [5]), ._06(\output [6]), ._07(\output [7]), ._08(\output [8]),
    ._09(\output [9]), .o10(\output [10]), .o11(\output [11]), .o12(\output [12]), .o13(\output [13]),
    .o14(\output [14]), ._015(\output [15]));  // open: Eo

  // Notes on the sheet:
  //   INC= D6 T5
  //   LD= (D0+D1+D2+D6)*T4
endmodule

module TR (
  input  AC_15,
  input  AC_0,
  input  I,
  input  S,
  input  E,
  input  R,
  input  IEN,
  input  FGI,
  input  FGO,
  input  T0,
  input  T1,
  input  T2,
  input  T3,
  input  T4,
  input  T5,
  input  T6,
  input  D0,
  input  D1,
  input  D2,
  input  D3,
  input  D4,
  input  D5,
  input  D6,
  input  D7,
  input  B0,
  input  B1,
  input  B2,
  input  B3,
  input  B4,
  input  B5,
  input  B6,
  input  B7,
  input  B8,
  input  B9,
  input  B10,
  input  B11,
  input  [15:0] \input ,
  output [15:0] \output 
);

  wire and_1_out, clock_1_out;

  Clock clock_1 (.out(clock_1_out));
  and and_1 (and_1_out, R, T0);
  _16_Bit_A_Register u_16_bit_a_register_1 (
    .Clear(1'b0), .Load(and_1_out), .Increment(1'b0), .i0(\input [0]), .i1(\input [1]), .i2(\input [2]),
    .i3(\input [3]), .i4(\input [4]), .i5(\input [5]), .i6(\input [6]), .i7(\input [7]), .i8(\input [8]),
    .i9(\input [9]), .i10(\input [10]), .i11(\input [11]), .i12(\input [12]), .i13(\input [13]),
    .i14(\input [14]), .i15(\input [15]), .Clk(clock_1_out), .o0(\output [0]), .o1(\output [1]),
    ._02(\output [2]), ._03(\output [3]), ._04(\output [4]), ._05(\output [5]), ._06(\output [6]),
    ._07(\output [7]), ._08(\output [8]), ._09(\output [9]), .o10(\output [10]), .o11(\output [11]),
    .o12(\output [12]), .o13(\output [13]), .o14(\output [14]), ._015(\output [15]));  // open: Eo

  // Notes on the sheet:
  //   LD= R T0
endmodule

// IR REG
module IR (
  input  AC_15,
  input  AC_0,
  input  I,
  input  S,
  input  E,
  input  R,
  input  IEN,
  input  FGI,
  input  FGO,
  input  T0,
  input  T1,
  input  T2,
  input  T3,
  input  T4,
  input  T5,
  input  T6,
  input  D0,
  input  D1,
  input  D2,
  input  D3,
  input  D4,
  input  D5,
  input  D6,
  input  D7,
  input  B0,
  input  B1,
  input  B2,
  input  B3,
  input  B4,
  input  B5,
  input  B6,
  input  B7,
  input  B8,
  input  B9,
  input  B10,
  input  B11,
  input  [15:0] \input ,
  output [15:0] \output 
);

  wire and_1_out, clock_1_out, not_1_out;

  Clock clock_1 (.out(clock_1_out));
  not not_1 (not_1_out, R);
  and and_1 (and_1_out, not_1_out, T1);
  _16_Bit_A_Register u_16_bit_a_register_1 (
    .Clear(1'b0), .Load(and_1_out), .Increment(1'b0), .i0(\input [0]), .i1(\input [1]), .i2(\input [2]),
    .i3(\input [3]), .i4(\input [4]), .i5(\input [5]), .i6(\input [6]), .i7(\input [7]), .i8(\input [8]),
    .i9(\input [9]), .i10(\input [10]), .i11(\input [11]), .i12(\input [12]), .i13(\input [13]),
    .i14(\input [14]), .i15(\input [15]), .Clk(clock_1_out), .o0(\output [0]), .o1(\output [1]),
    ._02(\output [2]), ._03(\output [3]), ._04(\output [4]), ._05(\output [5]), ._06(\output [6]),
    ._07(\output [7]), ._08(\output [8]), ._09(\output [9]), .o10(\output [10]), .o11(\output [11]),
    .o12(\output [12]), .o13(\output [13]), .o14(\output [14]), ._015(\output [15]));  // open: Eo

  // Notes on the sheet:
  //   LD=R' T1 
endmodule

module OUTR (
  input  AC_15,
  input  AC_0,
  input  I,
  input  S,
  input  E,
  input  R,
  input  IEN,
  input  FGI,
  input  FGO,
  input  T0,
  input  T1,
  input  T2,
  input  T3,
  input  T4,
  input  T5,
  input  T6,
  input  D0,
  input  D1,
  input  D2,
  input  D3,
  input  D4,
  input  D5,
  input  D6,
  input  D7,
  input  B0,
  input  B1,
  input  B2,
  input  B3,
  input  B4,
  input  B5,
  input  B6,
  input  B7,
  input  B8,
  input  B9,
  input  B10,
  input  B11,
  output [7:0] \output 
);

  wire and_1_out, and_2_out;

  Clock clock_1 ();  // open: out
  and and_1 (and_1_out, I, T3, D7);
  and and_2 (and_2_out, and_1_out, B10);
  _8_Bit_B_Reg u_8_bit_b_reg_1 (
    .Load(and_2_out), .o0(\output [0]), .o1(\output [1]), .o2(\output [2]), .o3(\output [3]),
    ._04(\output [4]), .o5(\output [5]), .o6(\output [6]), .o7(\output [7]));  // open: i0, i1, i2, i3, i4, i5, i6, i7, Clock

  // Notes on the sheet:
  //   LD= D7 I T3 B(10)
endmodule

module INPR (
  input  AC_15,
  input  AC_0,
  input  I,
  input  S,
  input  E,
  input  R,
  input  IEN,
  input  FGI,
  input  FGO,
  input  T0,
  input  T1,
  input  T2,
  input  T3,
  input  T4,
  input  T5,
  input  T6,
  input  D0,
  input  D1,
  input  D2,
  input  D3,
  input  D4,
  input  D5,
  input  D6,
  input  D7,
  input  B0,
  input  B1,
  input  B2,
  input  B3,
  input  B4,
  input  B5,
  input  B6,
  input  B7,
  input  B8,
  input  B9,
  input  B10,
  input  B11,
  input  [7:0] \input 
);

  Clock clock_1 ();  // open: out
  _8_Bit_B_Reg u_8_bit_b_reg_1 (
    .Load(1'b0), .i0(\input [0]), .i1(\input [1]), .i2(\input [2]), .i3(\input [3]), .i4(\input [4]),
    .i5(\input [5]), .i6(\input [6]), .i7(\input [7]));  // open: Clock, o0, o1, o2, o3, _04, o5, o6, o7
endmodule

module Memory (
  input  [11:0] Address,
  input  AC_15,
  input  AC_0,
  input  I,
  input  S,
  input  E,
  input  R,
  input  IEN,
  input  FGI,
  input  FGO,
  input  T0,
  input  T1,
  input  T2,
  input  T3,
  input  T4,
  input  T5,
  input  T6,
  input  D0,
  input  D1,
  input  D2,
  input  D3,
  input  D4,
  input  D5,
  input  D6,
  input  D7,
  input  B0,
  input  B1,
  input  B2,
  input  B3,
  input  B4,
  input  B5,
  input  B6,
  input  B7,
  input  B8,
  input  B9,
  input  B10,
  input  B11,
  input  [15:0] Data_in,
  output [15:0] Data_Out
);

  wire and_1_out, and_2_out, and_3_out, and_4_out, and_5_out, and_6_out, and_7_out, clock_1_out, or_1_out,
       or_2_out, or_3_out, undriven;

  Clock clock_1 (.out(clock_1_out));
  and and_1 (and_1_out, I, T3, ~D7);  // AND_Gate
  and and_2 (and_2_out, ~R, T1);  // AND_Gate
  buf and_3 (and_3_out, or_1_out);  // AND_Gate
  or or_1 (or_1_out, D2, D0, D1, D6);
  and and_4 (and_4_out, R, T1);
  and and_5 (and_5_out, T3, D3);
  and and_6 (and_6_out, T4, D5);
  and and_7 (and_7_out, T6, D6);
  or or_2 (or_2_out, and_4_out, and_5_out, and_6_out, and_7_out);
  or or_3 (or_3_out, and_2_out, and_1_out, and_3_out);
  RAM #(.addrWidth(12), .dataWidth(16), .bus("separate")) ram_1 (
    .addr(Address), .din(Data_in), .data(Data_Out), .str(or_2_out), .sel(undriven), .clk(clock_1_out),
    .ld(or_3_out));  // open: clr

  // Notes on the sheet:
  //   R T1
  //   D3 T3
  //    D7' I T3 
  //   D5 T4
  //   D6 T6
  //   R' T1
  //   (D0+D1+D6+D2)*T4
  //   MemRead=R' T1 + D7' I T3 + T4* (D0 + D1 + D2 +D6)
  //   MemWrt= R T1 + D3 T4 + D5 T4 + D6 T6
endmodule

module _1_Bit_ALU (
  input  in_1,
  input  in_2,
  output out_3,
  output out_4,
  output out_5
);

  Adder #(.width(1)) adder_1 (.a(in_1), .b(in_2), .out(out_3), .cout(out_4));  // open: cin
  and and_1 (out_5, in_1, in_2);
endmodule

module AC (
  input  AC_15,
  input  AC_0,
  input  I,
  input  S,
  input  E,
  input  R,
  input  IEN,
  input  FGI,
  input  FGO,
  input  T0,
  input  T1,
  input  T2,
  input  T3,
  input  T4,
  input  T5,
  input  T6,
  input  D0,
  input  D1,
  input  D2,
  input  D3,
  input  D4,
  input  D5,
  input  D6,
  input  D7,
  input  B0,
  input  B1,
  input  B2,
  input  B3,
  input  B4,
  input  B5,
  input  B6,
  input  B7,
  input  B8,
  input  B9,
  input  B10,
  input  B11,
  input  B15,
  input  [15:0] Input,
  output [15:0] \output 
);

  wire and_1_out, and_2_out, and_3_out, and_4_out, and_5_out, and_6_out, and_7_out, and_8_out, and_9_out,
       and_10_out, and_11_out, clock_1_out, or_1_out;

  Clock clock_1 (.out(clock_1_out));
  and and_1 (and_1_out, I, T3, D7);
  and and_2 (and_2_out, T5, D0);
  and and_3 (and_3_out, T5, D1);
  and and_4 (and_4_out, T5, D2);
  and and_5 (and_5_out, ~I, D7, T3);  // AND_Gate
  and and_6 (and_6_out, B11, and_5_out);
  and and_7 (and_7_out, and_5_out, B9);
  and and_8 (and_8_out, and_5_out, B7);
  and and_9 (and_9_out, and_5_out, B6);
  and and_10 (and_10_out, and_1_out, B11);
  and and_11 (and_11_out, B5, and_5_out);
  or or_1 (or_1_out, and_7_out, and_8_out, and_9_out, and_10_out, and_2_out, and_3_out, and_4_out);
  _16_Bit_A_Register u_16_bit_a_register_1 (
    .Clear(and_6_out), .Load(or_1_out), .Increment(and_11_out), .i0(Input[0]), .i1(Input[1]), .i2(Input[2]),
    .i3(Input[3]), .i4(Input[4]), .i5(Input[5]), .i6(Input[6]), .i7(Input[7]), .i8(Input[8]), .i9(Input[9]),
    .i10(Input[10]), .i11(Input[11]), .i12(Input[12]), .i13(Input[13]), .i14(Input[14]), .i15(Input[15]),
    .Clk(clock_1_out), .o0(AC_0), .o1(\output [1]), ._02(\output [2]), ._03(\output [3]), ._04(\output [4]),
    ._05(\output [5]), ._06(\output [6]), ._07(\output [7]), ._08(\output [8]), ._09(\output [9]),
    .o10(\output [10]), .o11(\output [11]), .o12(\output [12]), .o13(\output [13]), .o14(\output [14]),
    ._015(AC_15), .Eo(E));

  assign {\output [15], \output [0]} = {AC_15, AC_0};

  // Notes on the sheet:
  //   r=D7*I'*T3
  //   p=D7*I*T3
  //   D0*T5
  //   D1*T5
  //   D2*T5
  //   r*B9
  //   r*B7
  //   r*B6
  //   p*B11
  //   CLR=r*B11
  //   INC=r*B5
  //   LD=D0*T5+D1*T5+D2*T5+p*B11+r*B9+r*B7+r*B6
  //   ALU İLAVE EDİLECEK
endmodule

module FLAG_I (
  input  IR_15,
  input  AC_15,
  input  AC_0,
  input  I,
  input  S,
  input  E,
  input  R,
  input  IEN,
  input  FGI,
  input  FGO,
  input  T0,
  input  T1,
  input  T2,
  input  T3,
  input  T4,
  input  T5,
  input  T6,
  input  D0,
  input  D1,
  input  D2,
  input  D3,
  input  D4,
  input  D5,
  input  D6,
  input  D7,
  input  B0,
  input  B1,
  input  B2,
  input  B3,
  input  B4,
  input  B5,
  input  B6,
  input  B7,
  input  B8,
  input  B9,
  input  B10,
  input  B11
);

  wire and_1_out, and_2_out, clock_1_out;

  Clock clock_1 (.out(clock_1_out));
  and and_1 (and_1_out, ~R, T2);  // AND_Gate
  and and_2 (and_2_out, IR_15, and_1_out);
  D_Flip_Flop d_ff_1 (.clk(clock_1_out), .D(and_2_out), .Q(I));  // open: Qn, preset, en, reset

  // Notes on the sheet:
  //   I = R' T2 IR(15)
endmodule

module FLAG_S (
  input  AC_15,
  input  AC_0,
  input  I,
  input  S,
  input  E,
  input  R,
  input  IEN,
  input  FGI,
  input  FGO,
  input  T0,
  input  T1,
  input  T2,
  input  T3,
  input  T4,
  input  T5,
  input  T6,
  input  D0,
  input  D1,
  input  D2,
  input  D3,
  input  D4,
  input  D5,
  input  D6,
  input  D7,
  input  B0,
  input  B1,
  input  B2,
  input  B3,
  input  B4,
  input  B5,
  input  B6,
  input  B7,
  input  B8,
  input  B9,
  input  B10,
  input  B11
);

  wire and_1_out, and_2_out, clock_1_out;

  Clock clock_1 (.out(clock_1_out));
  and and_1 (and_1_out, ~I, T3, D7);  // AND_Gate
  and and_2 (and_2_out, and_1_out, B0);
  D_Flip_Flop d_ff_1 (.clk(clock_1_out), .D(and_2_out), .Q(S));  // open: Qn, preset, en, reset

  // Notes on the sheet:
  //   S= D7 I' T3 B(0)
endmodule

module FLAG_R (
  input  AC_15,
  input  AC_0,
  input  I,
  input  S,
  input  E,
  input  R,
  input  IEN,
  input  FGI,
  input  FGO,
  input  T0,
  input  T1,
  input  T2,
  input  T3,
  input  T4,
  input  T5,
  input  T6,
  input  D0,
  input  D1,
  input  D2,
  input  D3,
  input  D4,
  input  D5,
  input  D6,
  input  D7,
  input  B0,
  input  B1,
  input  B2,
  input  B3,
  input  B4,
  input  B5,
  input  B6,
  input  B7,
  input  B8,
  input  B9,
  input  B10,
  input  B11
);

  wire and_1_out, and_2_out, and_3_out, clock_1_out, not_1_out, not_2_out, not_3_out, or_1_out;

  not not_1 (not_1_out, T0);
  not not_2 (not_2_out, T1);
  not not_3 (not_3_out, T2);
  Clock clock_1 (.out(clock_1_out));
  or or_1 (or_1_out, FGI, FGO);
  and and_1 (and_1_out, not_1_out, not_2_out, not_3_out);
  and and_2 (and_2_out, IEN, or_1_out, and_1_out);
  buf and_3 (and_3_out, R);  // AND_Gate
  J_K_Flip_Flop j_k_ff_1 (.J(and_2_out), .clk(clock_1_out), .K(and_3_out), .Q(R));  // open: Qn, preset, en, reset

  // Notes on the sheet:
  //   R T2
  //   T0' T1' T2' (IEN) (FGI + FGO)
endmodule

module FLAG_IEN (
  input  AC_15,
  input  AC_0,
  input  I,
  input  S,
  input  E,
  input  R,
  input  IEN,
  input  FGI,
  input  FGO,
  input  T0,
  input  T1,
  input  T2,
  input  T3,
  input  T4,
  input  T5,
  input  T6,
  input  D0,
  input  D1,
  input  D2,
  input  D3,
  input  D4,
  input  D5,
  input  D6,
  input  D7,
  input  B0,
  input  B1,
  input  B2,
  input  B3,
  input  B4,
  input  B5,
  input  B6,
  input  B7,
  input  B8,
  input  B9,
  input  B10,
  input  B11
);

  wire and_1_out, and_2_out, and_3_out, and_4_out, clock_1_out, or_1_out;

  Clock clock_1 (.out(clock_1_out));
  and and_1 (and_1_out, I, T3, D7);
  and and_2 (and_2_out, and_1_out, B7);
  and and_3 (and_3_out, and_1_out, B6);
  and and_4 (and_4_out, R, T2);
  J_K_Flip_Flop j_k_ff_1 (.J(and_2_out), .clk(clock_1_out), .K(or_1_out), .Q(IEN));  // open: Qn, preset, en, reset
  or or_1 (or_1_out, and_3_out, and_4_out);

  // Notes on the sheet:
  //   p= D7 I T3
  //   p B(7)
  //   R T2 + B(6) p
endmodule

module FGI (
  input  AC_15,
  input  AC_0,
  input  I,
  input  S,
  input  E,
  input  R,
  input  IEN,
  input  FGI,
  input  FGO,
  input  T0,
  input  T1,
  input  T2,
  input  T3,
  input  T4,
  input  T5,
  input  T6,
  input  D0,
  input  D1,
  input  D2,
  input  D3,
  input  D4,
  input  D5,
  input  D6,
  input  D7,
  input  B0,
  input  B1,
  input  B2,
  input  B3,
  input  B4,
  input  B5,
  input  B6,
  input  B7,
  input  B8,
  input  B9,
  input  B10,
  input  B11
);

  wire and_1_out, and_2_out, clock_1_out;

  Clock clock_1 (.out(clock_1_out));
  and and_1 (and_1_out, I, T3, D7);
  and and_2 (and_2_out, and_1_out, B11);
  D_Flip_Flop d_ff_1 (.clk(clock_1_out), .D(and_2_out), .Q(FGI));  // open: Qn, preset, en, reset

  // Notes on the sheet:
  //   D7 I T3 B(11)
endmodule

module FGO (
  input  AC_15,
  input  AC_0,
  input  I,
  input  S,
  input  E,
  input  R,
  input  IEN,
  input  FGI,
  input  FGO,
  input  T0,
  input  T1,
  input  T2,
  input  T3,
  input  T4,
  input  T5,
  input  T6,
  input  D0,
  input  D1,
  input  D2,
  input  D3,
  input  D4,
  input  D5,
  input  D6,
  input  D7,
  input  B0,
  input  B1,
  input  B2,
  input  B3,
  input  B4,
  input  B5,
  input  B6,
  input  B7,
  input  B8,
  input  B9,
  input  B10,
  input  B11
);

  wire and_1_out, and_2_out, clock_1_out;

  Clock clock_1 (.out(clock_1_out));
  and and_1 (and_1_out, I, T3, D7);
  and and_2 (and_2_out, and_1_out, B10);
  D_Flip_Flop d_ff_1 (.clk(clock_1_out), .D(and_2_out), .Q(FGO));  // open: Qn, preset, en, reset

  // Notes on the sheet:
  //   D7 I T3 B(10)
endmodule

module FLAG_E (
  input  Co,
  input  IR_15,
  input  AC_15,
  input  AC_0,
  input  I,
  input  S,
  input  E,
  input  R,
  input  IEN,
  input  FGI,
  input  FGO,
  input  T0,
  input  T1,
  input  T2,
  input  T3,
  input  T4,
  input  T5,
  input  T6,
  input  D0,
  input  D1,
  input  D2,
  input  D3,
  input  D4,
  input  D5,
  input  D6,
  input  D7,
  input  B0,
  input  B1,
  input  B2,
  input  B3,
  input  B4,
  input  B5,
  input  B6,
  input  B7,
  input  B8,
  input  B9,
  input  B10,
  input  B11
);

  wire and_1_out, and_2_out, and_3_out, and_4_out, and_5_out, and_6_out, and_7_out, and_8_out, and_9_out,
       clock_1_out, j_k_ff_1_qn, or_1_out, or_2_out, or_3_out, or_4_out;

  Clock clock_1 (.out(clock_1_out));
  or or_1 (or_1_out, Co, j_k_ff_1_qn, AC_15, AC_0);
  and and_1 (and_1_out, ~I, T3, D7);  // AND_Gate
  and and_2 (and_2_out, and_1_out, B10);
  and and_3 (and_3_out, B8, and_1_out);
  and and_4 (and_4_out, and_1_out, B7);
  and and_5 (and_5_out, T5, D1);
  and and_6 (and_6_out, and_1_out, B6);
  or or_2 (or_2_out, and_3_out, and_4_out, and_5_out, and_6_out);
  and and_7 (and_7_out, ~and_2_out, and_3_out);  // AND_Gate
  and and_8 (and_8_out, ~and_2_out, or_2_out, or_1_out);  // AND_Gate
  and and_9 (and_9_out, or_2_out, ~or_1_out);  // AND_Gate
  or or_3 (or_3_out, and_7_out, and_8_out);
  or or_4 (or_4_out, and_9_out, and_2_out, and_3_out);
  J_K_Flip_Flop j_k_ff_1 (
    .J(or_3_out), .clk(clock_1_out), .K(or_4_out), .Q(E), .Qn(j_k_ff_1_qn));  // open: preset, en, reset

  // Notes on the sheet:
  //   r=D7 I' T3
  //   Input= AC(0) + AC(15) + C0 + E'
  //   CLR= r B(10) 
  //   Load=D1 T5 + r B7 + r B6 + r B8
  //   saat girişi LD olabilir mi ? 
  //   çalışmasını kontrol et !!
endmodule

// 7x3 encoder
module _7X3_Encoder (
  input  x1,
  input  x2,
  input  x3,
  input  x4,
  input  x5,
  input  x6,
  input  x7,
  output s0,
  output s1,
  output s2
);

  or or_1 (s0, x1, x3, x5, x7);
  or or_2 (s1, x2, x3, x6, x7);
  or or_3 (s2, x4, x5, x6, x7);
endmodule

// 1 Bit Bus
module _1_Ortak_bsus (
  input  _0,
  input  _1,
  input  _2,
  input  _3,
  input  _4,
  input  _5,
  input  _6,
  input  _7,
  input  [2:0] Select,
  output _0_2,
  output _1_2,
  output _2_2,
  output _3_2,
  output _4_2,
  output _5_2,
  output _6_2,
  output _7_2
);

  wire decoder_1_out0, decoder_1_out1, decoder_1_out2, decoder_1_out3, decoder_1_out4, decoder_1_out5,
       decoder_1_out6, decoder_1_out7;

  Decoder #(.select(3), .enable("false")) decoder_1 (
    .out0(decoder_1_out0), .out1(decoder_1_out1), .out2(decoder_1_out2), .out3(decoder_1_out3),
    .out4(decoder_1_out4), .out5(decoder_1_out5), .out6(decoder_1_out6), .out7(decoder_1_out7), .sel(Select));
  assign _0_2 = decoder_1_out0 ? _0 : 1'bz;  // Controlled_Buffer controlled_buffer_1
  assign _1_2 = decoder_1_out1 ? _1 : 1'bz;  // Controlled_Buffer controlled_buffer_2
  assign _2_2 = decoder_1_out2 ? _2 : 1'bz;  // Controlled_Buffer controlled_buffer_3
  assign _3_2 = decoder_1_out3 ? _3 : 1'bz;  // Controlled_Buffer controlled_buffer_4
  assign _4_2 = decoder_1_out4 ? _4 : 1'bz;  // Controlled_Buffer controlled_buffer_5
  assign _5_2 = decoder_1_out5 ? _5 : 1'bz;  // Controlled_Buffer controlled_buffer_6
  assign _6_2 = decoder_1_out6 ? _6 : 1'bz;  // Controlled_Buffer controlled_buffer_7
  assign _7_2 = decoder_1_out7 ? _7 : 1'bz;  // Controlled_Buffer controlled_buffer_8
endmodule

// bus select
module BUS_SELEC (
  input  I,
  input  S,
  input  E,
  input  R,
  input  IEN,
  input  FGI,
  input  FGO,
  input  T0,
  input  T1,
  input  T2,
  input  T3,
  input  T4,
  input  T5,
  input  T6,
  input  D0,
  input  D1,
  input  D2,
  input  D3,
  input  D4,
  input  D5,
  input  D6,
  input  D7,
  output AR,
  output PC,
  output DR,
  output AC,
  output IR,
  output TR,
  output MemRead
);

  wire and_1_out, and_2_out, and_3_out, and_4_out, and_5_out, and_6_out, and_7_out, and_8_out, and_9_out,
       and_10_out, and_11_out, and_12_out, and_13_out, or_1_out, or_2_out, or_3_out, or_4_out, or_5_out;
  wire [2:0] n7x3_encoder_1_s0;

  and and_1 (and_1_out, T4, D4);
  and and_2 (and_2_out, T5, D5);
  and and_3 (and_3_out, ~R, T0);  // AND_Gate
  and and_4 (and_4_out, T4, D5);
  and and_5 (and_5_out, T5, D2);
  and and_6 (and_6_out, T6, D6);
  and and_7 (and_7_out, R, T0);
  or or_1 (or_1_out, and_1_out, and_2_out);
  or or_2 (or_2_out, and_3_out, and_7_out, and_4_out);
  or or_3 (or_3_out, and_5_out, and_6_out);
  and and_8 (and_8_out, ~R, T2);  // AND_Gate
  and and_9 (and_9_out, I, T3, D7);
  and and_10 (and_10_out, T4, or_4_out);
  or or_4 (or_4_out, D0, D2, D1, D6);
  and and_11 (and_11_out, R, T1);
  and and_12 (and_12_out, T4, D3);
  and and_13 (and_13_out, ~R, T1);  // AND_Gate
  or or_5 (or_5_out, and_13_out, and_9_out, and_10_out);
  _7X3_Encoder u_7x3_encoder_1 (
    .x1(or_1_out), .x2(or_2_out), .x3(or_3_out), .x4(and_12_out), .x5(and_8_out), .x6(and_11_out),
    .x7(or_5_out), .s0(n7x3_encoder_1_s0[0]), .s1(n7x3_encoder_1_s0[1]), .s2(n7x3_encoder_1_s0[2]));
  Decoder #(.select(3)) decoder_1 (
    .out1(AR), .out2(PC), .out3(DR), .out4(AC), .out5(IR), .out6(TR), .out7(MemRead), .sel(n7x3_encoder_1_s0));  // open: out0, en

  // Notes on the sheet:
  //   AC= D3*T4
  //   IR= R’*T2
  //   TR= R*T1
  //   AR=D4*T4+D5*T5
  //   PC= R’*T0 + RT0 + D5*T4 
  //   DR= D2*T5 + D6*T6
  //   MemRead= R’*T1+D7'*I*T3+T4*(D0+D1+D2+D6)
  //   ** AC'nin belirli bitleri fonksiyona dahil edilmedi.
endmodule

module Control_Unit (
  input  SC_INC,
  input  SC_CLR,
  output D0,
  output D1,
  output D2,
  output D3,
  output D4,
  output D5,
  output D6,
  output D7,
  output T0,
  output T1,
  output T2,
  output T3,
  output T4,
  output T5,
  output T6,
  output T7,
  output T8,
  output T9,
  output T10,
  output T11,
  output T12,
  output T13,
  output T14,
  output T15
);

  wire clock_1_out, j_k_ff_1_q, j_k_ff_2_q, j_k_ff_3_q;
  wire [3:0] j_k_ff_1_qn;
  wire [15:0] ir_1_output;

  Clock clock_1 (.out(clock_1_out));
  J_K_Flip_Flop j_k_ff_1 (
    .J(1'b1), .clk(clock_1_out), .K(1'b1), .Q(j_k_ff_1_q), .Qn(j_k_ff_1_qn[0]), .en(SC_INC), .reset(SC_CLR));  // open: preset
  IR ir_1 (.\output (ir_1_output));  // open: AC_15, AC_0, I, S, E, R, IEN, FGI, FGO, T0, T1, T2, T3, T4, T5, T6, D0, D1, D2, D3, D4, D5, D6, D7, B0, B1, B2, B3, B4, B5, B6, B7, B8, B9, B10, B11, input
  Decoder #(.select(4)) decoder_1 (
    .out0(T0), .out1(T1), .out2(T2), .out3(T3), .out4(T4), .out5(T5), .out6(T6), .out7(T7), .out8(T8),
    .out9(T9), .out10(T10), .out11(T11), .out12(T12), .out13(T13), .out14(T14), .out15(T15), .sel(j_k_ff_1_qn));  // open: en
  J_K_Flip_Flop j_k_ff_2 (
    .J(1'b1), .clk(j_k_ff_1_q), .K(1'b1), .Q(j_k_ff_2_q), .Qn(j_k_ff_1_qn[1]), .en(SC_INC), .reset(SC_CLR));  // open: preset
  J_K_Flip_Flop j_k_ff_3 (
    .J(1'b1), .clk(j_k_ff_2_q), .K(1'b1), .Q(j_k_ff_3_q), .Qn(j_k_ff_1_qn[2]), .en(SC_INC), .reset(SC_CLR));  // open: preset
  Decoder #(.select(3)) decoder_2 (
    .out0(D7), .out1(D6), .out2(D5), .out3(D4), .out4(D3), .out5(D2), .out6(D1), .out7(D0),
    .sel(ir_1_output[14:12]));  // open: en
  J_K_Flip_Flop j_k_ff_4 (
    .J(1'b1), .clk(j_k_ff_3_q), .K(1'b1), .Qn(j_k_ff_1_qn[3]), .en(SC_INC), .reset(SC_CLR));  // open: Q, preset

  // Notes on the sheet:
  //   OPERATION
  //   TIMING
endmodule

module ALU (
  input  LD,
  input  CLK,
  input  AND,
  input  ADD,
  input  DR,
  input  INPR,
  input  COM,
  input  SHR,
  input  SHL,
  input  AC_0,
  input  AC_1,
  input  AC_2,
  input  AC_3,
  input  AC_4,
  input  AC_5,
  input  AC_6,
  input  AC_7,
  input  AC_8,
  input  AC_9,
  input  AC_10,
  input  AC_11,
  input  AC_12,
  input  AC_13,
  input  AC_14,
  input  AC_15,
  input  DR_0,
  input  DR_1,
  input  DR_2,
  input  DR_3,
  input  DR_4,
  input  DR_5,
  input  DR_6,
  input  DR_7,
  input  DR_8,
  input  DR_9,
  input  DR_10,
  input  DR_11,
  input  DR_12,
  input  DR_13,
  input  DR_14,
  input  DR_15,
  input  INPR_0,
  input  INPR_1,
  input  INPR_2,
  input  INPR_3,
  input  INPR_4,
  input  INPR_5,
  input  INPR_6,
  input  INPR_7,
  output _0,
  output _1,
  output _2,
  output _3,
  output _4,
  output _5,
  output _6,
  output _7,
  output _8,
  output _9,
  output _10,
  output _11,
  output _12,
  output _13,
  output _14,
  output _15
);

  wire ADD_2_out, ADD_3_out, ADD_4_out, ADD_5_out, ADD_6_out, ADD_7_out, ADD_8_out, ADD_9_out, ADD_10_out,
       ADD_11_out, ADD_12_out, ADD_13_out, ADD_14_out, ADD_15_out, ADD_16_out, ADD_out, AND_2_out, AND_3_out,
       AND_4_out, AND_5_out, AND_6_out, AND_7_out, AND_8_out, AND_9_out, AND_10_out, AND_11_out, AND_12_out,
       AND_13_out, AND_14_out, AND_15_out, AND_16_out, and_17_out, and_18_out, and_19_out, and_20_out,
       and_21_out, and_22_out, and_23_out, and_24_out, and_25_out, and_26_out, and_27_out, and_28_out,
       and_29_out, and_30_out, and_31_out, and_32_out, AND_out, COM_2_out, COM_3_out, COM_4_out, COM_5_out,
       COM_6_out, COM_7_out, COM_8_out, COM_9_out, COM_10_out, COM_11_out, COM_12_out, COM_13_out,
       COM_14_out, COM_15_out, COM_16_out, COM_out, DR_2_out, DR_3_out, DR_4_out, DR_5_out, DR_6_out,
       DR_7_out, DR_8_out, DR_9_out, DR_10_out, DR_11_out, DR_12_out, DR_13_out, DR_14_out, DR_15_out,
       DR_16_out, DR_out, I_0_out, I_1_out, I_2_out, I_3_out, I_4_out, I_5_out, I_6_out, I_7_out, INPR_2_out,
       INPR_3_out, INPR_4_out, INPR_5_out, INPR_6_out, INPR_7_out, INPR_8_out, INPR_9_out, INPR_10_out,
       INPR_11_out, INPR_12_out, INPR_13_out, INPR_14_out, INPR_15_out, INPR_16_out, INPR_out, SHL_2_out,
       SHL_3_out, SHL_4_out, SHL_5_out, SHL_6_out, SHL_7_out, SHL_8_out, SHL_9_out, SHL_10_out, SHL_11_out,
       SHL_12_out, SHL_13_out, SHL_14_out, SHL_15_out, SHL_16_out, SHL_out, SHR_2_out, SHR_3_out, SHR_4_out,
       SHR_5_out, SHR_6_out, SHR_7_out, SHR_8_out, SHR_9_out, SHR_10_out, SHR_11_out, SHR_12_out, SHR_13_out,
       SHR_14_out, SHR_15_out, SHR_16_out, SHR_out;

  buf u_AND (AND_out, AND);  // AND_Gate
  buf u_ADD (ADD_out, ADD);  // AND_Gate
  buf u_DR (DR_out, DR);  // AND_Gate
  buf u_INPR (INPR_out, INPR);  // AND_Gate
  buf u_COM (COM_out, COM);  // AND_Gate AND_Gate
  buf u_SHR (SHR_out, SHR);  // AND_Gate
  buf u_SHL (SHL_out, SHL);  // AND_Gate
  buf AND_2 (AND_2_out, AND);  // AND_Gate
  buf ADD_2 (ADD_2_out, ADD);  // AND_Gate
  buf u_DR_2 (DR_2_out, DR);  // AND_Gate
  buf u_INPR_2 (INPR_2_out, INPR);  // AND_Gate
  buf COM_2 (COM_2_out, COM);  // AND_Gate AND_Gate
  buf SHR_2 (SHR_2_out, SHR);  // AND_Gate
  buf SHL_2 (SHL_2_out, SHL);  // AND_Gate
  buf AND_3 (AND_3_out, AND);  // AND_Gate
  buf ADD_3 (ADD_3_out, ADD);  // AND_Gate
  buf u_DR_3 (DR_3_out, DR);  // AND_Gate
  buf u_INPR_3 (INPR_3_out, INPR);  // AND_Gate
  buf COM_3 (COM_3_out, COM);  // AND_Gate AND_Gate
  buf SHR_3 (SHR_3_out, SHR);  // AND_Gate
  buf SHL_3 (SHL_3_out, SHL);  // AND_Gate
  buf AND_4 (AND_4_out, AND);  // AND_Gate
  buf ADD_4 (ADD_4_out, ADD);  // AND_Gate
  buf u_DR_4 (DR_4_out, DR);  // AND_Gate
  buf u_INPR_4 (INPR_4_out, INPR);  // AND_Gate
  buf COM_4 (COM_4_out, COM);  // AND_Gate AND_Gate
  buf SHR_4 (SHR_4_out, SHR);  // AND_Gate
  buf SHL_4 (SHL_4_out, SHL);  // AND_Gate
  buf AND_5 (AND_5_out, AND);  // AND_Gate
  buf ADD_5 (ADD_5_out, ADD);  // AND_Gate
  buf u_DR_5 (DR_5_out, DR);  // AND_Gate
  buf u_INPR_5 (INPR_5_out, INPR);  // AND_Gate
  buf COM_5 (COM_5_out, COM);  // AND_Gate AND_Gate
  buf SHR_5 (SHR_5_out, SHR);  // AND_Gate
  buf SHL_5 (SHL_5_out, SHL);  // AND_Gate
  buf AND_6 (AND_6_out, AND);  // AND_Gate
  buf ADD_6 (ADD_6_out, ADD);  // AND_Gate
  buf u_DR_6 (DR_6_out, DR);  // AND_Gate
  buf u_INPR_6 (INPR_6_out, INPR);  // AND_Gate
  buf COM_6 (COM_6_out, COM);  // AND_Gate AND_Gate
  buf SHR_6 (SHR_6_out, SHR);  // AND_Gate
  buf SHL_6 (SHL_6_out, SHL);  // AND_Gate
  buf AND_7 (AND_7_out, AND);  // AND_Gate
  buf ADD_7 (ADD_7_out, ADD);  // AND_Gate
  buf u_DR_7 (DR_7_out, DR);  // AND_Gate
  buf u_INPR_7 (INPR_7_out, INPR);  // AND_Gate
  buf COM_7 (COM_7_out, COM);  // AND_Gate AND_Gate
  buf SHR_7 (SHR_7_out, SHR);  // AND_Gate
  buf SHL_7 (SHL_7_out, SHL);  // AND_Gate
  buf AND_8 (AND_8_out, AND);  // AND_Gate
  buf ADD_8 (ADD_8_out, ADD);  // AND_Gate
  buf u_DR_8 (DR_8_out, DR);  // AND_Gate
  buf INPR_8 (INPR_8_out, INPR);  // AND_Gate
  buf COM_8 (COM_8_out, COM);  // AND_Gate AND_Gate
  buf SHR_8 (SHR_8_out, SHR);  // AND_Gate
  buf SHL_8 (SHL_8_out, SHL);  // AND_Gate
  buf AND_9 (AND_9_out, AND);  // AND_Gate
  buf ADD_9 (ADD_9_out, ADD);  // AND_Gate
  buf u_DR_9 (DR_9_out, DR);  // AND_Gate
  buf INPR_9 (INPR_9_out, INPR);  // AND_Gate
  buf COM_9 (COM_9_out, COM);  // AND_Gate AND_Gate
  buf SHR_9 (SHR_9_out, SHR);  // AND_Gate
  buf SHL_9 (SHL_9_out, SHL);  // AND_Gate
  buf AND_10 (AND_10_out, AND);  // AND_Gate
  buf ADD_10 (ADD_10_out, ADD);  // AND_Gate
  buf u_DR_10 (DR_10_out, DR);  // AND_Gate
  buf INPR_10 (INPR_10_out, INPR);  // AND_Gate
  buf COM_10 (COM_10_out, COM);  // AND_Gate AND_Gate
  buf SHR_10 (SHR_10_out, SHR);  // AND_Gate
  buf SHL_10 (SHL_10_out, SHL);  // AND_Gate
  buf AND_11 (AND_11_out, AND);  // AND_Gate
  buf ADD_11 (ADD_11_out, ADD);  // AND_Gate
  buf u_DR_11 (DR_11_out, DR);  // AND_Gate
  buf INPR_11 (INPR_11_out, INPR);  // AND_Gate
  buf COM_11 (COM_11_out, COM);  // AND_Gate AND_Gate
  buf SHR_11 (SHR_11_out, SHR);  // AND_Gate
  buf SHL_11 (SHL_11_out, SHL);  // AND_Gate
  buf AND_12 (AND_12_out, AND);  // AND_Gate
  buf ADD_12 (ADD_12_out, ADD);  // AND_Gate
  buf u_DR_12 (DR_12_out, DR);  // AND_Gate
  buf INPR_12 (INPR_12_out, INPR);  // AND_Gate
  buf COM_12 (COM_12_out, COM);  // AND_Gate AND_Gate
  buf SHR_12 (SHR_12_out, SHR);  // AND_Gate
  buf SHL_12 (SHL_12_out, SHL);  // AND_Gate
  buf AND_13 (AND_13_out, AND);  // AND_Gate
  buf ADD_13 (ADD_13_out, ADD);  // AND_Gate
  buf u_DR_13 (DR_13_out, DR);  // AND_Gate
  buf INPR_13 (INPR_13_out, INPR);  // AND_Gate
  buf COM_13 (COM_13_out, COM);  // AND_Gate AND_Gate
  buf SHR_13 (SHR_13_out, SHR);  // AND_Gate
  buf SHL_13 (SHL_13_out, SHL);  // AND_Gate
  buf AND_14 (AND_14_out, AND);  // AND_Gate
  buf ADD_14 (ADD_14_out, ADD);  // AND_Gate
  buf u_DR_14 (DR_14_out, DR);  // AND_Gate
  buf INPR_14 (INPR_14_out, INPR);  // AND_Gate
  buf COM_14 (COM_14_out, COM);  // AND_Gate AND_Gate
  buf SHR_14 (SHR_14_out, SHR);  // AND_Gate
  buf SHL_14 (SHL_14_out, SHL);  // AND_Gate
  buf AND_15 (AND_15_out, AND);  // AND_Gate
  buf ADD_15 (ADD_15_out, ADD);  // AND_Gate
  buf u_DR_15 (DR_15_out, DR);  // AND_Gate
  buf INPR_15 (INPR_15_out, INPR);  // AND_Gate
  buf COM_15 (COM_15_out, COM);  // AND_Gate AND_Gate
  buf SHR_15 (SHR_15_out, SHR);  // AND_Gate
  buf SHL_15 (SHL_15_out, SHL);  // AND_Gate
  buf AND_16 (AND_16_out, AND);  // AND_Gate
  buf ADD_16 (ADD_16_out, ADD);  // AND_Gate
  buf DR_16 (DR_16_out, DR);  // AND_Gate
  buf INPR_16 (INPR_16_out, INPR);  // AND_Gate
  buf COM_16 (COM_16_out, COM);  // AND_Gate AND_Gate
  buf SHR_16 (SHR_16_out, SHR);  // AND_Gate
  buf SHL_16 (SHL_16_out, SHL);  // AND_Gate
  or I_0 (I_0_out, AND_out, ADD_out, DR_out, INPR_out, COM_out, SHR_out, SHL_out);
  or I_1 (I_1_out, AND_2_out, ADD_2_out, DR_2_out, INPR_2_out, COM_2_out, SHR_2_out, SHL_2_out);
  or I_2 (I_2_out, AND_3_out, ADD_3_out, DR_3_out, INPR_3_out, COM_3_out, SHR_3_out, SHL_3_out);
  or I_3 (I_3_out, AND_4_out, ADD_4_out, DR_4_out, INPR_4_out, COM_4_out, SHR_4_out, SHL_4_out);
  or I_4 (I_4_out, AND_5_out, ADD_5_out, DR_5_out, INPR_5_out, COM_5_out, SHR_5_out, SHL_5_out);
  or I_5 (I_5_out, AND_6_out, ADD_6_out, DR_6_out, INPR_6_out, COM_6_out, SHR_6_out, SHL_6_out);
  or I_6 (I_6_out, AND_7_out, ADD_7_out, DR_7_out, INPR_7_out, COM_7_out, SHR_7_out, SHL_7_out);
  or I_7 (I_7_out, AND_8_out, ADD_8_out, DR_8_out, INPR_8_out, COM_8_out, SHR_8_out, SHL_8_out);
  // OR_Gate I_8 has open pins: in0=AND_9_out, in1=ADD_9_out, in2=DR_9_out, in3=INPR_9_out, in4=COM_9_out, in5=SHR_9_out, in6=SHL_9_out, out=open
  // OR_Gate I_9 has open pins: in0=AND_10_out, in1=ADD_10_out, in2=DR_10_out, in3=INPR_10_out, in4=COM_10_out, in5=SHR_10_out, in6=SHL_10_out, out=open
  // OR_Gate I_10 has open pins: in0=AND_11_out, in1=ADD_11_out, in2=DR_11_out, in3=INPR_11_out, in4=COM_11_out, in5=SHR_11_out, in6=SHL_11_out, out=open
  // OR_Gate I_11 has open pins: in0=AND_12_out, in1=ADD_12_out, in2=DR_12_out, in3=INPR_12_out, in4=COM_12_out, in5=SHR_12_out, in6=SHL_12_out, out=open
  // OR_Gate I_12 has open pins: in0=AND_13_out, in1=ADD_13_out, in2=DR_13_out, in3=INPR_13_out, in4=COM_13_out, in5=SHR_13_out, in6=SHL_13_out, out=open
  // OR_Gate I_13 has open pins: in0=AND_14_out, in1=ADD_14_out, in2=DR_14_out, in3=INPR_14_out, in4=COM_14_out, in5=SHR_14_out, in6=SHL_14_out, out=open
  // OR_Gate I_14 has open pins: in0=AND_15_out, in1=ADD_15_out, in2=DR_15_out, in3=INPR_15_out, in4=COM_15_out, in5=SHR_15_out, in6=SHL_15_out, out=open
  // OR_Gate I_15 has open pins: in0=AND_16_out, in1=ADD_16_out, in2=DR_16_out, in3=INPR_16_out, in4=COM_16_out, in5=SHR_16_out, in6=SHL_16_out, out=open
  and and_17 (and_17_out, LD, I_0_out);
  and and_18 (and_18_out, ~I_0_out, LD);  // AND_Gate
  and and_19 (and_19_out, LD, I_1_out);
  and and_20 (and_20_out, ~I_1_out, LD);  // AND_Gate
  and and_21 (and_21_out, LD, I_2_out);
  and and_22 (and_22_out, ~I_2_out, LD);  // AND_Gate
  and and_23 (and_23_out, LD, I_3_out);
  and and_24 (and_24_out, ~I_3_out, LD);  // AND_Gate
  and and_25 (and_25_out, LD, I_4_out);
  and and_26 (and_26_out, ~I_4_out, LD);  // AND_Gate
  and and_27 (and_27_out, LD, I_5_out);
  and and_28 (and_28_out, ~I_5_out, LD);  // AND_Gate
  and and_29 (and_29_out, LD, I_6_out);
  and and_30 (and_30_out, ~I_6_out, LD);  // AND_Gate
  and and_31 (and_31_out, LD, I_7_out);
  and and_32 (and_32_out, ~I_7_out, LD);  // AND_Gate
  J_K_Flip_Flop j_k_ff_1 (.J(and_17_out), .clk(CLK), .K(and_18_out), .Q(_0));  // open: Qn, preset, en, reset
  J_K_Flip_Flop j_k_ff_2 (.J(and_19_out), .clk(CLK), .K(and_20_out), .Q(_1));  // open: Qn, preset, en, reset
  J_K_Flip_Flop j_k_ff_3 (.J(and_21_out), .clk(CLK), .K(and_22_out), .Q(_2));  // open: Qn, preset, en, reset
  J_K_Flip_Flop j_k_ff_4 (.J(and_23_out), .clk(CLK), .K(and_24_out), .Q(_3));  // open: Qn, preset, en, reset
  J_K_Flip_Flop j_k_ff_5 (.J(and_25_out), .clk(CLK), .K(and_26_out));  // open: Q, Qn, preset, en, reset
  J_K_Flip_Flop j_k_ff_6 (.J(and_27_out), .clk(CLK), .K(and_28_out));  // open: Q, Qn, preset, en, reset
  J_K_Flip_Flop j_k_ff_7 (.J(and_29_out), .clk(CLK), .K(and_30_out));  // open: Q, Qn, preset, en, reset
  J_K_Flip_Flop j_k_ff_8 (.J(and_31_out), .clk(CLK), .K(and_32_out));  // open: Q, Qn, preset, en, reset

  // Notes on the sheet:
  //   ****   AC(i-1) için hangi giriş olmalı
endmodule
